# Fritzing sketch circuit_view (saved by Fritzing 0.9.3b)
breadboards: 1

parts:
  Parça1 = Arduino Mega 2560 (Rev3)
  HC-SR04_Sensor_1 = HC-SR04 Ultrasonic Distance Sensor
  U1 = LCD-16X2 [package=lcd-16x2]
  U2 = POT [package=pot_alpha_rv16af-20]
  U3 = POT [package=pot_alpha_rv16af-20]
  U4 = POT [package=pot_alpha_rv16af-20]
  U5 = POT [package=pot_alpha_rv16af-20]
  S1 = Pushbutton [package="[SMD]"]
  S2 = Pushbutton [package="[SMD]"]
  S3 = Pushbutton [package="[SMD]"]
  U6 = BATTERY-2 [package=battery-aa]
  U7 = BATTERY-2 [package=battery-aa]
  U9 = BATTERY-2 [package=battery-aa]
  U10 = BATTERY-2 [package=battery-aa]
  U11 = BATTERY-2 [package=battery-aa]
  U12 = BATTERY-2 [package=battery-aa]
  U13 = BATTERY-2 [package=battery-aa]
  U14 = BATTERY-2 [package=battery-aa]
  Part1 = LED Matrix - Serial Interface - Red/Green/Blue
  U15 = L298 [package=multiwatt15_6400bgheatsink]
  M1 = DC Motor

nets:
  N1: Parça1.A0, U5.S
  N2: Parça1.A1, U4.S
  N3: Parça1.A2, U2.S
  GND: Parça1.GND, HC-SR04_Sensor_1.GND, U1.VSS, U1.R_W, U1.K, U2.A, U3.A, U4.A, U5.A, S1.Pin_3, S1.Pin_4, S2.Pin_3, S2.Pin_4, S3.Pin_3, S3.Pin_4, U6.-1, Part1.GND, U15.GND
  N4: Parça1.D13_PWM, Part1.CS
  N5: Parça1.D12_PWM, Part1.SCK
  N6: Parça1.D11_PWM, Part1.MOSI
  VCC: Parça1.5V, HC-SR04_Sensor_1.VCC, U1.VDD, U1.A, U2.E, U3.E, U4.E, U5.E, Part1.VCC
  N7: Parça1.D2_PWM, HC-SR04_Sensor_1.ECHO
  N8: Parça1.D3_PWM, HC-SR04_Sensor_1.TRIG
  N9: Parça1.D4_PWM, S1.Pin_1, S1.Pin_2
  N10: Parça1.D5_PWM, S3.Pin_1, S3.Pin_2
  N11: Parça1.D6_PWM, S2.Pin_1, S2.Pin_2
  N12: Parça1.D7_PWM, U15.ENA
  N13: Parça1.D22, U15.IN2
  N14: Parça1.D24, U15.IN1
  N15: Parça1.D42, U1.DB7
  N16: Parça1.D44, U1.DB6
  N17: Parça1.D46, U1.DB5
  N18: Parça1.D48, U1.DB4
  N19: Parça1.D50, U1.E
  N20: Parça1.D52, U1.RS
  N21: U1.VO, U3.S
  N22: U6.+1, U7.-1
  N23: U7.+1, U10.-1
  N24: U9.-1, U10.+1
  N25: U9.+1, U11.-1
  N26: U11.+1, U14.-1
  N27: U12.-1, U14.+1
  N28: U12.+1, U13.-1
  N29: U13.+1, U15.VS
  N30: U15.OUT1, M1.pin_2
  N31: U15.OUT2, M1.pin_1
